// Logisim project sequential-hex-counter.circ as structural Verilog: 1 circuit, main circuit main
module main (
);

  wire and_1_out, and_2_out, and_3_out, and_4_out, and_5_out, and_6_out, and_7_out, and_8_out, and_9_out,
       and_10_out, clock_1_out, or_1_out, or_2_out, or_3_out, or_4_out, or_5_out, or_6_out, xnor_1_out,
       xnor_2_out, xnor_3_out, xor_1_out;
  wire [2:0] j_k_ff_1_q, t_ff_3_q;

  Clock clock_1 (.out(clock_1_out));
  and and_1 (and_1_out, and_5_out, t_ff_3_q[2]);
  or or_1 (or_1_out, and_1_out, and_2_out);
  and and_2 (and_2_out, ~and_5_out, t_ff_3_q[1], t_ff_3_q[0]);  // AND_Gate
  T_Flip_Flop t_ff_1 (.clk(clock_1_out), .T(or_1_out), .Q(t_ff_3_q[2]));  // open: Qn, preset, reset, en
  and and_3 (and_3_out, ~and_5_out, t_ff_3_q[0]);  // AND_Gate
  or or_2 (or_2_out, and_3_out, and_4_out);
  and and_4 (and_4_out, and_5_out, t_ff_3_q[1]);
  T_Flip_Flop t_ff_2 (.clk(clock_1_out), .T(or_2_out), .Q(t_ff_3_q[1]));  // open: Qn, preset, reset, en
  or or_3 (or_3_out, t_ff_3_q[0], ~and_5_out);  // OR_Gate
  T_Flip_Flop t_ff_3 (.clk(clock_1_out), .T(or_3_out), .Q(t_ff_3_q[0]));  // open: Qn, preset, reset, en
  Hex_Digit_Display hex_digit_display_1 (.value({1'b0, t_ff_3_q}));  // open: dp
  Hex_Digit_Display hex_digit_display_2 (.value({1'b0, j_k_ff_1_q}));  // open: dp
  xnor xnor_1 (xnor_1_out, t_ff_3_q[2], j_k_ff_1_q[2]);
  xnor xnor_2 (xnor_2_out, t_ff_3_q[1], j_k_ff_1_q[1]);
  and and_5 (and_5_out, xnor_1_out, xnor_2_out, xnor_3_out);
  xnor xnor_3 (xnor_3_out, t_ff_3_q[0], j_k_ff_1_q[0]);
  or or_4 (or_4_out, xor_1_out, and_6_out);
  xor xor_1 (xor_1_out, and_5_out, j_k_ff_1_q[2]);
  D_Flip_Flop d_ff_1 (.clk(clock_1_out), .D(or_4_out), .Q(j_k_ff_1_q[2]));  // open: Qn, preset, en, reset
  and and_6 (and_6_out, and_5_out, ~j_k_ff_1_q[0]);  // AND_Gate
  or or_5 (or_5_out, and_7_out, and_8_out);
  and and_7 (and_7_out, and_5_out, ~j_k_ff_1_q[1], j_k_ff_1_q[0]);  // AND_Gate
  and and_8 (and_8_out, and_5_out, ~j_k_ff_1_q[2], j_k_ff_1_q[0]);  // AND_Gate
  T_Flip_Flop t_ff_4 (.clk(clock_1_out), .T(or_5_out), .Q(j_k_ff_1_q[1]));  // open: Qn, preset, reset, en
  or or_6 (or_6_out, and_9_out, and_10_out);
  and and_9 (and_9_out, and_5_out, ~j_k_ff_1_q[1]);  // AND_Gate
  J_K_Flip_Flop j_k_ff_1 (
    .J(and_5_out), .clk(clock_1_out), .K(or_6_out), .Q(j_k_ff_1_q[0]));  // open: Qn, preset, en, reset
  and and_10 (and_10_out, and_5_out, ~j_k_ff_1_q[2]);  // AND_Gate
endmodule
