// Logisim project seven-segment-name-display.circ as structural Verilog: 1 circuit, main circuit main
module main (
);

  wire _0_out, _1_out, _2_out, _3_out, _4_out, _5_out, _6_out, _7_out, _8_out, _9_out, _10_out, _11_out,
       _12_out, _13_out, _14_out, _15_out, A_out, a_prime_b_out, a_prime_bc_prime_out, a_prime_c_out,
       a_prime_cd_prime_2_out, a_prime_cd_prime_out, a_xnor_c_out, a_xor_c_2_out, a_xor_c_out, a_xor_d_out,
       ab_prime_c_2_out, ab_prime_c_out, ab_prime_c_prime_out, ab_prime_d_out, ac_prime_out, B_out,
       b_prime_c_out, b_prime_d_bd_prime_out, b_xor_d_out, bc_prime_d_prime_out, bc_prime_out, bd_prime_out,
       c__a_xor_d_out, C_out, c_prime_b_prime_d_bd_prime_out, c_prime_d_out, cd_prime_out, d_a_xnor_c_out,
       D_out, d_prime_c_xor_a_out, E_out, F_out, G_out;
  wire [3:0] priority_encoder_1_out;

  Button _0 (.out(_0_out));
  Button _1 (.out(_1_out));
  Button _2 (.out(_2_out));
  Button _3 (.out(_3_out));
  Button _4 (.out(_4_out));
  Button _5 (.out(_5_out));
  Button _6 (.out(_6_out));
  Button _7 (.out(_7_out));
  Button _8 (.out(_8_out));
  Button _9 (.out(_9_out));
  Button _10 (.out(_10_out));
  Button _11 (.out(_11_out));
  Button _12 (.out(_12_out));
  Button _13 (.out(_13_out));
  Button _14 (.out(_14_out));
  Button _15 (.out(_15_out));
  Priority_Encoder #(.select(4)) priority_encoder_1 (
    .in0(_0_out), .in1(_1_out), .in2(_2_out), .in3(_3_out), .in4(_4_out), .in5(_5_out), .in6(_6_out),
    .in7(_7_out), .in8(_8_out), .in9(_9_out), .in10(_10_out), .in11(_11_out), .in12(_12_out), .in13(_13_out),
    .in14(_14_out), .in15(_15_out), .out(priority_encoder_1_out));  // open: gs, en_out, en_in
  and a_prime_cd_prime (a_prime_cd_prime_out, ~priority_encoder_1_out[3], priority_encoder_1_out[1], ~priority_encoder_1_out[0]);  // AND_Gate
  xor b_prime_d_bd_prime (b_prime_d_bd_prime_out, priority_encoder_1_out[2], priority_encoder_1_out[0]);
  and bc_prime_d_prime (bc_prime_d_prime_out, priority_encoder_1_out[2], ~priority_encoder_1_out[1], ~priority_encoder_1_out[0]);  // AND_Gate
  and a_prime_cd_prime_2 (a_prime_cd_prime_2_out, ~priority_encoder_1_out[3], priority_encoder_1_out[1], ~priority_encoder_1_out[0]);  // AND_Gate
  and ab_prime_c (ab_prime_c_out, priority_encoder_1_out[3], ~priority_encoder_1_out[2], priority_encoder_1_out[1]);  // AND_Gate
  xor a_xor_d (a_xor_d_out, priority_encoder_1_out[3], priority_encoder_1_out[0]);
  and ab_prime_d (ab_prime_d_out, priority_encoder_1_out[3], ~priority_encoder_1_out[2], priority_encoder_1_out[0]);  // AND_Gate
  xor a_xor_c (a_xor_c_out, priority_encoder_1_out[3], priority_encoder_1_out[1]);
  and a_prime_c (a_prime_c_out, ~priority_encoder_1_out[3], priority_encoder_1_out[1]);  // AND_Gate
  and ab_prime_c_prime (ab_prime_c_prime_out, priority_encoder_1_out[3], ~priority_encoder_1_out[2], ~priority_encoder_1_out[1]);  // AND_Gate
  and bd_prime (bd_prime_out, priority_encoder_1_out[2], ~priority_encoder_1_out[0]);  // AND_Gate
  and c_prime_b_prime_d_bd_prime (c_prime_b_prime_d_bd_prime_out, ~priority_encoder_1_out[1], b_prime_d_bd_prime_out);  // AND_Gate
  xor a_xor_c_2 (a_xor_c_2_out, priority_encoder_1_out[3], priority_encoder_1_out[1]);
  xnor a_xnor_c (a_xnor_c_out, priority_encoder_1_out[3], priority_encoder_1_out[1]);
  and a_prime_bc_prime (a_prime_bc_prime_out, ~priority_encoder_1_out[3], priority_encoder_1_out[2], ~priority_encoder_1_out[1]);  // AND_Gate
  and c__a_xor_d (c__a_xor_d_out, a_xor_d_out, priority_encoder_1_out[1]);
  xor b_xor_d (b_xor_d_out, priority_encoder_1_out[2], priority_encoder_1_out[0]);
  and bc_prime (bc_prime_out, priority_encoder_1_out[2], ~priority_encoder_1_out[1]);  // AND_Gate
  and cd_prime (cd_prime_out, priority_encoder_1_out[1], ~priority_encoder_1_out[0]);  // AND_Gate
  and c_prime_d (c_prime_d_out, ~priority_encoder_1_out[1], priority_encoder_1_out[0]);  // AND_Gate
  and ac_prime (ac_prime_out, priority_encoder_1_out[3], ~priority_encoder_1_out[1]);  // AND_Gate
  and b_prime_c (b_prime_c_out, ~priority_encoder_1_out[2], priority_encoder_1_out[1]);  // AND_Gate
  and a_prime_b (a_prime_b_out, ~priority_encoder_1_out[3], priority_encoder_1_out[2]);  // AND_Gate
  and d_a_xnor_c (d_a_xnor_c_out, a_xnor_c_out, priority_encoder_1_out[0]);
  and d_prime_c_xor_a (d_prime_c_xor_a_out, a_xor_c_2_out, ~priority_encoder_1_out[0]);  // AND_Gate
  and ab_prime_c_2 (ab_prime_c_2_out, priority_encoder_1_out[3], ~priority_encoder_1_out[2], priority_encoder_1_out[1]);  // AND_Gate
  or A (A_out, a_prime_cd_prime_out, c_prime_b_prime_d_bd_prime_out);
  or B (B_out, bc_prime_d_prime_out, a_prime_cd_prime_2_out, ab_prime_c_out);
  or C (C_out, d_prime_c_xor_a_out, d_a_xnor_c_out, ab_prime_c_2_out, a_prime_bc_prime_out);
  or D (D_out, c__a_xor_d_out, ab_prime_d_out);
  or E (E_out, b_xor_d_out, bc_prime_out, a_xor_c_out);
  or F (F_out, a_prime_c_out, bd_prime_out, cd_prime_out, ab_prime_c_prime_out);
  or G (G_out, c_prime_d_out, b_prime_c_out, ac_prime_out, a_prime_b_out);
  _7_Segment_Display u_7_segment_display_1 (
    .g(G_out), .f(F_out), .a(A_out), .b(B_out), .e(E_out), .d(D_out), .c(C_out));  // open: dp

  // Notes on the sheet:
  //   M
  //   A
  //   T
  //   A
  //   A
  //   T
  //   H
  //   E
  //   Y
  //   D
  //   A
  //   R
  //   N
  //   L
  //   I
endmodule
